# Fritzing sketch cryptopi (saved by Fritzing 0.9.3b)
breadboards: 1

parts:
  Raspberry_Pi_1 = Raspberry Pi 3 [part_number=RPI-3-V1.2]
  LCD1 = LCD screen
  PIR1 = PIR sensor
  R1 = Trimmer Potentiometer [maximum_resistance=10kΩ package=THT]
  Part1 = NeoPixel Stick [part_number=1426]  # not connected

nets:
  N1: Raspberry_Pi_1.GIPO11, LCD1.DB3
  N2: Raspberry_Pi_1.GIPO5, LCD1.DB2
  N3: Raspberry_Pi_1.GIPO6, LCD1.DB1
  N4: Raspberry_Pi_1.GIPO13, LCD1.DB0
  N5: Raspberry_Pi_1.GIPO19, LCD1.E
  N6: Raspberry_Pi_1.GIPO26, LCD1.RS
  N7: Raspberry_Pi_1.GIPO14, PIR1.SIG
  GND: Raspberry_Pi_1.GND, LCD1.VSS, LCD1.R/W, LCD1.LED-, PIR1.GND, R1.leg2
  VDD: Raspberry_Pi_1.5V, LCD1.VDD, LCD1.LED+, PIR1.VDD, R1.leg1
  N8: LCD1.V0, R1.wiper

custom parts:
  NeoPixel Stick: Make your own little LED strip arrangement with this stick of NeoPixel LEDs. We crammed 8 of the tiny 5050 (5mm x 5mm) smart RGB LEDs onto a PCB with mounting holes and a chainable design. Use only one microcontroller pin to control as many as you can chain together! Each LED is addressable as the driver chip is inside the LED. Each one has ~18mA constant current drive so the color will be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
